// Logisim project logic gates.circ as structural Verilog: 1 circuit, main circuit main
module main (
);

  wire and_1_out, nand_1_out, nor_1_out, not_1_out, or_1_out, undriven, undriven_2, undriven_3, undriven_4,
       undriven_5, undriven_6, undriven_7, undriven_8, undriven_9, undriven_10, undriven_11, undriven_12,
       undriven_13, xnor_1_out, xor_1_out;

  not not_1 (not_1_out, undriven);
  or or_1 (or_1_out, undriven_2, undriven_3);
  nor nor_1 (nor_1_out, undriven_4, undriven_5);
  xnor xnor_1 (xnor_1_out, undriven_6, undriven_7);
  and and_1 (and_1_out, undriven_8, undriven_9);
  nand nand_1 (nand_1_out, undriven_10, undriven_11);
  xor xor_1 (xor_1_out, undriven_12, undriven_13);
endmodule
